# Fritzing sketch LedBoard (saved by Fritzing 0.9.3b)
circuit board: 4.99922cm x 1.5cm
breadboards: 1

parts:
  LED1 = LED - 5mm [color="Red (633nm)" package="5 mm [THT]"]
  LED2 = LED - 5mm [color="Red (633nm)" package="5 mm [THT]"]
  LED3 = LED - 5mm [color="Red (633nm)" package="5 mm [THT]"]
  LED4 = LED - 5mm [color="Red (633nm)" package="5 mm [THT]"]
  J1 = female pin header, 1 pin [form="♀ (female)"]

nets:
  N1: LED1.anode, LED2.anode, LED3.anode, LED4.anode, J1.pin1
