# Fritzing sketch Rifle (saved by Fritzing 0.9.3b)
breadboards: 1

parts:
  Q1 = NPN-Transistor [package="TO92 [THT]"]
  U1 = PIC-ICSP-Mini [package=pic-icsp-mini]
  S1 = Pushbutton [package="[THT]"]
  Q2 = LTR-301 [package=ltr-301]
  S2 = Pushbutton [package="[THT]"]
  R1 = Resistor [tolerance=±5% resistance=10k package=THT]
  R2 = Resistor [tolerance=±5% resistance=10k package=THT]

nets:
  N1: Q1.E, Q2.C
  N2: Q1.B, U1.VPP
  N3: Q1.C, U1.PGC, S1.Pin_1, S1.Pin_2, S2.Pin_1, S2.Pin_2, R1.Pin_1, R2.Pin_1
  N4: U1.VCC, S2.Pin_3, S2.Pin_4
  N5: U1.GND, S1.Pin_3, S1.Pin_4
  N6: U1.PGD, Q2.E, R1.Pin_0, R2.Pin_0

notes:
  D3|D8|D9|GND|5V
