# Fritzing sketch Receiver (saved by Fritzing 0.9.3b)
circuit board: 4.49504cm x 4.20604cm
breadboards: 1

parts:
  U1 = PIC-ICSP-Mini [package=pic-icsp-mini]
  LED1 = smd LED [color="Red (633nm)" package="0805 [SMD]"]
  R1 = Resistor [tolerance=±5% resistance=220 package=THT]
  LED2 = smd LED [color="Red (633nm)" package="0805 [SMD]"]
  R2 = Resistor [tolerance=±5% resistance=220 package=THT]
  LED3 = smd LED [color="Red (633nm)" package="0805 [SMD]"]
  LED4 = smd LED [color="Red (633nm)" package="0805 [SMD]"]
  R3 = Resistor [tolerance=±5% resistance=220 package=THT]
  R4 = Resistor [tolerance=±5% resistance=220 package=THT]
  IR1 = TSOP312.., 314.. [package=THT]
  U2 = PIC-ICSP-Mini [package=pic-icsp-mini]

nets:
  N1: U1.VPP, LED4.anode, R4.Pin_0, R4.Pin_1
  N2: U1.VCC, LED3.anode, R3.Pin_0, R3.Pin_1
  N3: U1.GND, LED2.anode, R2.Pin_0, R2.Pin_1
  N4: U1.PGD, LED1.anode, R1.Pin_0, R1.Pin_1
  N5: U1.PGC, LED1.cathode, LED2.cathode, LED3.cathode, LED4.cathode, IR1.GND
  N6: IR1.Vs, U2.PGD
  N7: IR1.Data, U2.PGC

notes:
  5V|D2||D10-13|GND
