# Fritzing sketch RifleBoard (saved by Fritzing 0.9.3b)
circuit board: 8.46667cm x 5.64444cm
breadboards: 2

parts:
  Q1 = NPN-Transistor [package="TO92 [THT]"]
  D1 = LTE-302 [package=lte-302]
  S1 = Pushbutton [package="[THT]"]
  R1 = Resistor [tolerance=±5% resistance=10k package=THT]
  S2 = Pushbutton [package="[THT]"]
  R2 = Resistor [tolerance=±5% resistance=10k package=THT]
  Part1 = Arduino Uno (Rev3)
  IR1 = TSOP312.., 314.. [package=THT]
  R3 = Resistor [tolerance=±5% resistance=220 package=THT]
  LED1 = LEDs [package=led10mm]
  R4 = Resistor [tolerance=±5% resistance=220 package=THT]
  LED2 = LEDs [package=led10mm]
  R5 = Resistor [tolerance=±5% resistance=220 package=THT]
  LED3 = LEDs [package=led10mm]
  R6 = Resistor [tolerance=±5% resistance=220 package=THT]
  LED4 = LEDs [package=led10mm]

nets:
  N1: Q1.E, D1.A
  N2: Q1.B, Part1.D3_PWM
  N3: Q1.C, S1.Pin_1, S1.Pin_2, S2.Pin_1, S2.Pin_2, R2.Pin_1, Part1.5V, IR1.Vs
  GND: D1.C, R1.Pin_0, R2.Pin_0, Part1.GND, IR1.GND, LED1.A, LED2.A, LED3.A, LED4.A
  N4: S1.Pin_3, S1.Pin_4, R1.Pin_1, Part1.D9_PWM
  N5: S2.Pin_3, S2.Pin_4, Part1.D8
  N6: Part1.D10_PWM/SS, R6.Pin_0
  N7: Part1.D11_PWM/MOSI, R5.Pin_0
  N8: Part1.D12/MISO, R4.Pin_0
  N9: Part1.D13/SCK, R3.Pin_0
  N10: Part1.D2, IR1.Data
  N11: R3.Pin_1, LED1.C
  N12: R4.Pin_1, LED2.C
  N13: R5.Pin_1, LED3.C
  N14: R6.Pin_1, LED4.C
