# Fritzing sketch RifleNEW (saved by Fritzing 0.9.3b)
circuit board: 8.46667cm x 5.64444cm
breadboards: 1

parts:
  Part1 = Arduino Nano (Rev3.0)
  J1 = female pin header, 5 pins [form="♀ (female)"]
  R1 = Resistor [tolerance=±5% resistance=220 package=THT]
  R2 = Resistor [tolerance=±5% resistance=220 package=THT]
  R3 = Resistor [tolerance=±5% resistance=220 package=THT]
  R4 = Resistor [tolerance=±5% resistance=220 package=THT]

nets:
  N1: Part1.D3, R1.Pin_0
  N2: Part1.D4, R2.Pin_0
  N3: Part1.D5, R3.Pin_0
  N4: Part1.D6, R4.Pin_0
  N5: Part1.GND, J1.pin1
  N6: J1.pin2, R1.Pin_1
  N7: J1.pin3, R2.Pin_1
  N8: J1.pin4, R3.Pin_1
  N9: J1.pin5, R4.Pin_1
